// Logisim project Arch242_Part_B.circ as structural Verilog: 9 circuits, main circuit main
module main (
);

  wire ACCWrite, ALUCF_out, and_3_out, and_4_out, CF, CFRead, CFWrite, Clk, clock_1_out, comparator_2_eq,
       comparator_4_eq, comparator_6_eq, comparator_7_eq, comparator_9_eq, comparator_10_eq,
       comparator_11_eq, comparator_12_eq, In2ndByteState, Is2ByteInst, is_b, is_bbit, is_call, is_ret,
       IsABCD, IsImmInst, IsShutdown, not_1_out, not_2_out, not_3_out, not_4_out, not_5_out, or_1_out, PCSel,
       PCWrite, RealACCWE, TempWE;
  wire [1:0] MemWrite, MemWriteSrc, PCWriteSrc, RegWriteSrc, TempWrite;
  wire [2:0] ALUSrcA, ALUSrcB, BranchCond;
  wire [3:0] ACC, ACCData, ACCWriteSrc, ALU_A, ALU_B, ALUResult, HiNibble, ImmA, ImmB, Inst, IOA,
       MemReadData, MemWriteData, PC_Hi4, RA, RB, RC, RD, RE, RegData, RegRead, RegToBeRead, RegWrite;
  wire [5:0] ALUOp;
  wire [7:0] BranchImm, InstCodeHigh, InstWord, MemAddr, undriven;
  wire [15:0] adder_1_out, ALUPC_out, ALUTemp_out, BranchTarget, IncValue, multiplexer_3_out, PC, TEMP;

  Clock clock_1 (.out(clock_1_out));
  Comparator comparator_1 (.a({HiNibble, Inst}), .b(8'h37), .eq(IsShutdown));  // open: gt, lt
  Multiplexer multiplexer_1 (.in0(clock_1_out), .in1(1'b0), .out(Clk), .sel(IsShutdown));
  // Probe on PC
  // Probe on PC
  PCReg pcreg_1 (
    .Clk(Clk), .PCSel(PCSel), .BranchAddr(BranchTarget), .IncValue(IncValue), .IsRet(is_ret),
    .AluTempOut(ALUPC_out), .PC_Out(PC), .PC_Hi4(PC_Hi4));
  Multiplexer #(.width(8)) multiplexer_2 (.in0(undriven), .in1(BranchImm), .out(InstWord), .sel(In2ndByteState));
  PCLogic pclogic_1 (
    .PCIn(PC), .InstrWord({InstCodeHigh, InstWord}), .ACC_out(ACC), .CF_out(CF), .RegA_out(RA),
    .RegB_out(RB), .TEMP_out(TEMP), .Is2ByteInst(Is2ByteInst), .Prelim_PCSel(PCWrite),
    .BranchType(BranchCond), .Is2ndByteState(In2ndByteState), .is_bbit(is_bbit), .is_b(is_b),
    .is_call(is_call), .IncValue(IncValue), .BranchTarget(BranchTarget), .PCSel(PCSel));  // open: TempRead
  // Probe on BranchTarget
  // Probe on PCSel
  // Probe on InstWord
  // Probe on InstCodeHigh
  Comparator #(.mode("unsigned"), .width(4)) comparator_2 (
    .a(InstCodeHigh[7:4]), .b(4'b1110), .eq(comparator_2_eq));  // open: gt, lt
  not not_1 (not_1_out, In2ndByteState);
  Comparator #(.mode("unsigned"), .width(4)) comparator_3 (
    .a(InstCodeHigh[7:4]), .b(4'b1111), .eq(is_call));  // open: gt, lt
  not not_2 (not_2_out, In2ndByteState);
  Comparator #(.mode("unsigned"), .width(3)) comparator_4 (
    .a(InstCodeHigh[7:5]), .b(3'b100), .eq(comparator_4_eq));  // open: gt, lt
  not not_3 (not_3_out, In2ndByteState);
  Comparator #(.mode("unsigned")) comparator_5 (.a({HiNibble, Inst}), .b(8'h2e), .eq(is_ret));  // open: gt, lt
  // Probe on {InstCodeHigh, InstWord}
  // Probe on {InstCodeHigh, InstWord}
  and and_1 (is_b, comparator_2_eq, not_1_out);
  and and_2 (is_bbit, comparator_4_eq, not_3_out);
  // Probe on {HiNibble, Inst}
  InstrMem instrmem_1 (.Address(PC), .Instr({HiNibble, Inst}));
  maindecoder maindecoder_1 (
    .InstCode({HiNibble, Inst}), .in_2(Clk), .PC(PC), .ALUOp(ALUOp), .ALUSrcA(ALUSrcA), .ALUSrcB(ALUSrcB),
    .CFRead(CFRead), .CFWrite(CFWrite), .ACCWrite(ACCWrite), .ACCWriteSrc(ACCWriteSrc), .RegRead(RegRead),
    .RegWrite(RegWrite), .RegWriteSrc(RegWriteSrc), .MemWrite(MemWrite), .MemWriteSrc(MemWriteSrc),
    .PCWrite(PCWrite), .PCWriteSrc(PCWriteSrc), .BranchCond(BranchCond), .TempWrite(TempWrite),
    .IsABCD(IsABCD), .ImmA(ImmA), .ImmB(ImmB), .Is2ByteInst(Is2ByteInst), .In2ndByteState(In2ndByteState),
    .BranchImm(BranchImm), .InstCodeHigh(InstCodeHigh));
  // Probe on BranchImm
  // Probe on {HiNibble, Inst}
  // Probe on RegWriteSrc
  // Probe on MemWrite
  // Probe on MemWriteSrc
  // Probe on PCWrite
  // Probe on PCWriteSrc
  // Probe on BranchCond
  // Probe on TempWrite
  // Probe on IsABCD
  // Probe on ALUOp
  // Probe on ALUSrcA
  // Probe on ALUSrcB
  // Probe on CFRead
  // Probe on CFWrite
  // Probe on ACCWrite
  // Probe on ACCWriteSrc
  // Probe on RegRead
  // Probe on RegWrite
  // Probe on TempWrite
  // Probe on ImmA
  // Probe on ImmB
  // Probe on Is2ByteInst
  // Probe on In2ndByteState
  Adder #(.width(16)) adder_1 (.a(PC), .b(16'h1), .out(adder_1_out));  // open: cin, cout
  Register #(.width(4)) u_IOA (.clk(Clk), .Q(IOA));  // open: D, en, clr
  // Probe on ACCData
  Multiplexer #(.width(16)) multiplexer_3 (
    .in0(ALUTemp_out), .in1(adder_1_out), .out(multiplexer_3_out), .sel(is_call));
  Register #(.width(4)) u_ACC (.D(ACCData), .en(RealACCWE), .clk(Clk), .Q(ACC));  // open: clr
  Register #(.width(16)) u_TEMP (.D(multiplexer_3_out), .en(TempWE), .clk(Clk), .Q(TEMP));  // open: clr
  RegisterFile registerfile_1 (
    .RegData(RegData), .RegWrite(RegWrite), .CFWrite(CFWrite), .CFData(ALUCF_out), .Clock(Clk),
    .IsABCD(IsABCD), .HiNibble(HiNibble), .RA_out(RA), .RB_out(RB), .RC_out(RC), .RD_out(RD), .RE_out(RE),
    .CF_out(CF));
  // Probe on ACC
  // Probe on ACC
  // Probe on TEMP
  // Probe on RA
  // Probe on RB
  // Probe on RC
  // Probe on RD
  // Probe on RE
  // Probe on CF
  Multiplexer #(.select(4), .width(4)) multiplexer_4 (
    .in0(MemReadData), .in1(MemReadData), .in2(ALUResult), .in3(RegToBeRead), .in4(ImmA), .in5(IOA),
    .out(ACCData), .sel(ACCWriteSrc));  // open: in6, in7, in8, in9, in10, in11, in12, in13, in14, in15
  Multiplexer multiplexer_5 (.in0(ACCWrite), .in1(1'b0), .out(RealACCWE), .sel(IsImmInst));
  Multiplexer #(.select(3), .width(4)) multiplexer_6 (
    .in0(ACC), .in1(MemReadData), .in2(MemReadData), .in3(RegToBeRead), .out(ALU_A), .sel(ALUSrcA));  // open: in4, in5, in6, in7
  Comparator #(.mode("unsigned"), .width(2)) comparator_6 (
    .a(TempWrite), .b(2'b00), .eq(comparator_6_eq));  // open: gt, lt
  // Probe on RegToBeRead
  Multiplexer #(.select(4), .width(4)) multiplexer_7 (
    .in1(RA), .in2(RB), .in3(RC), .in4(RD), .in5(RE), .in6(IOA), .out(RegToBeRead), .sel(RegRead));  // open: in0, in7, in8, in9, in10, in11, in12, in13, in14, in15
  not not_4 (not_4_out, comparator_6_eq);
  ALU alu_1 (
    .A(ALU_A), .B(ALU_B), .ALUOp(ALUOp), .CFe(CFRead), .CF_in(CF), .PC_in(PC), .Temp_in(TEMP),
    .Result(ALUResult), .CF_out(ALUCF_out), .PC_out(ALUPC_out), .Temp_out(ALUTemp_out));
  // Probe on ALUPC_out
  not not_5 (not_5_out, comparator_7_eq);
  Comparator #(.mode("unsigned"), .width(2)) comparator_7 (
    .a(TempWrite), .b(2'b00), .eq(comparator_7_eq));  // open: gt, lt
  and and_3 (and_3_out, not_4_out, In2ndByteState);
  // Probe on ALUResult
  // Probe on ALUTemp_out
  Comparator #(.mode("unsigned"), .width(4)) comparator_8 (.a(HiNibble), .b(4'b0100), .eq(IsImmInst));  // open: gt, lt
  Multiplexer #(.select(3), .width(4)) multiplexer_8 (
    .in1(MemReadData), .in2(ImmB), .in3(4'b0001), .in4(MemReadData), .out(ALU_B), .sel(ALUSrcB));  // open: in0, in5, in6, in7
  Multiplexer #(.select(2), .width(4)) multiplexer_9 (
    .in0(ACC), .in1(ALUResult), .in2(ImmB), .out(RegData), .sel(RegWriteSrc));  // open: in3
  Multiplexer multiplexer_10 (.in0(not_5_out), .in1(and_3_out), .out(TempWE), .sel(is_call));
  // Probe on MemAddr
  // Probe on MemWriteData
  Comparator #(.mode("unsigned"), .width(4)) comparator_9 (
    .a(ACCWriteSrc), .b(4'b0000), .eq(comparator_9_eq));  // open: gt, lt
  Comparator #(.mode("unsigned"), .width(3)) comparator_10 (
    .a(ALUSrcB), .b(3'b100), .eq(comparator_10_eq));  // open: gt, lt
  Comparator #(.mode("unsigned"), .width(3)) comparator_11 (
    .a(ALUSrcA), .b(3'b001), .eq(comparator_11_eq));  // open: gt, lt
  Comparator #(.mode("unsigned"), .width(2)) comparator_12 (
    .a(MemWrite), .b(2'b01), .eq(comparator_12_eq));  // open: gt, lt
  Multiplexer #(.select(2), .width(4)) multiplexer_11 (
    .in1(ALUResult), .in2(ACC), .out(MemWriteData), .sel(MemWriteSrc));  // open: in0, in3
  and and_4 (and_4_out, ACCWrite, comparator_9_eq);
  // Probe on MemReadData
  DataMem datamem_1 (.Addr(MemAddr), .MemWrite(MemWrite), .Data_in(MemWriteData), .Clk(Clk), .Data_out(MemReadData));
  or or_1 (or_1_out, and_4_out, comparator_10_eq, comparator_11_eq, comparator_12_eq);
  Multiplexer #(.width(8)) multiplexer_12 (.in0({RD, RC}), .in1({RB, RA}), .out(MemAddr), .sel(or_1_out));

  // Other names for the same wires on the sheet: LoNibble[3:0] = Inst; Inst[7:4] = HiNibble;
  //   InstWord[15:8] = InstCodeHigh; RBRA[7:0] = {RB, RA}; RDRC[7:0] = {RD, RC}

  // Notes on the sheet:
  //   Clock
  //   PC
  //   Fetch/Decode
  //   Registers
  //   Register Helpers
  //   ALU
  //   ALU Helpers
  //   Memory
  //   Memory Helpers
endmodule

module RegisterFile (
  input  [3:0] RegData,
  input  [3:0] RegWrite,
  input  CFWrite,
  input  CFData,
  input  Clock,
  input  IsABCD,
  input  [3:0] HiNibble,
  output [3:0] RA_out,
  output [3:0] RB_out,
  output [3:0] RC_out,
  output [3:0] RD_out,
  output [3:0] RE_out,
  output CF_out
);

  wire and_1_out, and_2_out, and_3_out, and_4_out, and_5_out, and_6_out, comparator_1_eq, comparator_2_eq,
       normalRA_e, normalRB_e, normalRC_e, normalRD_e, RA_e, RARB, RB_e, RC_e, RCRD, RD_e, RE_e, zRA_e,
       zRB_e, zRC_e, zRD_e;

  Decoder #(.select(4)) decoder_1 (
    .out1(normalRA_e), .out2(normalRB_e), .out3(normalRC_e), .out4(normalRD_e), .out5(RE_e), .out6(RARB),
    .out7(RCRD), .sel(RegWrite));  // open: out0, out8, out9, out10, out11, out12, out13, out14, out15, en
  Comparator #(.mode("unsigned"), .width(4)) comparator_1 (
    .a(HiNibble), .b(4'b0101), .eq(comparator_1_eq));  // open: gt, lt
  Comparator #(.mode("unsigned"), .width(4)) comparator_2 (
    .a(HiNibble), .b(4'b0110), .eq(comparator_2_eq));  // open: gt, lt
  and and_1 (and_1_out, comparator_1_eq, RARB);
  and and_2 (and_2_out, comparator_2_eq, RCRD);
  Demultiplexer demultiplexer_1 (.out0(zRB_e), .out1(zRA_e), .in(1'b1), .sel(and_1_out));
  Demultiplexer demultiplexer_2 (.out0(zRD_e), .out1(zRC_e), .in(1'b1), .sel(and_2_out));
  Register #(.width(4)) RA (.D(RegData), .en(RA_e), .clk(Clock), .Q(RA_out));  // open: clr
  Register #(.width(4)) RB (.D(RegData), .en(RB_e), .clk(Clock), .Q(RB_out));  // open: clr
  Register #(.width(4)) RC (.D(RegData), .en(RC_e), .clk(Clock), .Q(RC_out));  // open: clr
  Register #(.width(4)) RD (.D(RegData), .en(RD_e), .clk(Clock), .Q(RD_out));  // open: clr
  Register #(.width(4)) RE (.D(RegData), .en(RE_e), .clk(Clock), .Q(RE_out));  // open: clr
  Register #(.width(1)) CF (.D(CFData), .en(CFWrite), .clk(Clock), .Q(CF_out));  // open: clr
  and and_3 (and_3_out, RARB, IsABCD);
  Multiplexer multiplexer_1 (.in0(normalRA_e), .in1(zRA_e), .out(RA_e), .sel(and_3_out));
  Multiplexer multiplexer_2 (.in0(normalRC_e), .in1(zRC_e), .out(RC_e), .sel(and_4_out));
  and and_4 (and_4_out, RCRD, IsABCD);
  Multiplexer multiplexer_3 (.in0(normalRB_e), .in1(zRB_e), .out(RB_e), .sel(and_5_out));
  and and_5 (and_5_out, RARB, IsABCD);
  Multiplexer multiplexer_4 (.in0(normalRD_e), .in1(zRD_e), .out(RD_e), .sel(and_6_out));
  and and_6 (and_6_out, RCRD, IsABCD);

  // Other names for the same wires on the sheet: CF_e = CFWrite; DataIn[3:0] = RegData
endmodule

module InstrMem (
  input  [15:0] Address,
  output [7:0] Instr
);

  // Probe on Address
  ROM #(.addrWidth(16)) rom_1 (.addr(Address), .data(Instr));

  // Notes on the sheet:
  //   contents of rom_1 (hex, n*v repeats v):
  //   71 40 2 41 1 42 3 44 4 43 5 0 1 2 3 31 3f 5 4 c 7 6 f 10 46 9 5c 3 21 23 6d 4 25 29 2a 2b 88 27 a0
  //   28 b0 29 c8 2a e0 2c f0 2e 2e 37 3e
endmodule

module ALU (
  input  [3:0] A,
  input  [3:0] B,
  input  [5:0] ALUOp,
  input  CFe,
  input  CF_in,
  input  [15:0] PC_in,
  input  [15:0] Temp_in,
  output [3:0] Result,
  output CF_out,
  output [15:0] PC_out,
  output [15:0] Temp_out
);

  wire addCF_out, bcdCF_out, bcdEnable, comparator_1_gt, multiplexer_1_out, subCF_out;
  wire [3:0] adder_2_out, adder_3_out, addRes, andRes, bcdRes, orRes, subRes, subtractor_1_out, xorRes;

  // Probe on A
  // Probe on CF_in
  // Probe on A
  Multiplexer multiplexer_1 (.in0(1'b0), .in1(CF_in), .out(multiplexer_1_out), .sel(CFe));
  Adder #(.width(4)) adder_1 (.a(A), .b(B), .out(addRes), .cin(multiplexer_1_out), .cout(addCF_out));
  Subtractor #(.width(4)) subtractor_1 (.a(A), .b(B), .out(subtractor_1_out), .bout(subCF_out));  // open: bin
  assign andRes = A & B;  // AND_Gate and_1, 4 bits wide
  assign xorRes = A ^ B;  // XOR_Gate xor_1, 4 bits wide
  assign orRes = A | B;  // OR_Gate or_1, 4 bits wide
  // Probe on A[0]
  // Probe on subtractor_1_out
  // Probe on {CF_in, A[3:1]}
  // Probe on {A[2:0], CF_in}
  // Probe on adder_2_out
  Adder #(.width(4)) adder_2 (.a(subtractor_1_out), .b({3'b000, CF_in}), .out(adder_2_out));  // open: cin, cout
  Multiplexer #(.width(4)) multiplexer_2 (.in0(subtractor_1_out), .in1(adder_2_out), .out(subRes), .sel(CFe));
  Adder #(.width(4)) adder_3 (.a(A), .b(4'b0110), .out(adder_3_out));  // open: cin, cout
  Comparator #(.mode("unsigned"), .width(4)) comparator_1 (.a(A), .b(4'b1001), .gt(comparator_1_gt));  // open: eq, lt
  Multiplexer #(.width(4)) multiplexer_3 (.in0(A), .in1(adder_3_out), .out(bcdRes), .sel(bcdEnable));
  Multiplexer multiplexer_4 (.in0(CF_in), .in1(1'b1), .out(bcdCF_out), .sel(bcdEnable));
  or or_2 (bcdEnable, comparator_1_gt, CF_in);
  // Probe on PC_in[15:12]
  // Probe on ALUOp[4:0]
  Multiplexer #(.select(5), .width(4)) multiplexer_5 (
    .in1(addRes), .in2(subRes), .in3(andRes), .in4(xorRes), .in5(orRes), .in6({A[0], A[3:1]}),
    .in7({A[2:0], A[3]}), .in8({CF_in, A[3:1]}), .in9({A[2:0], CF_in}), .in10(bcdRes), .out(Result),
    .sel(ALUOp[4:0]));  // open: in0, in11, in12, in13, in14, in15, in16, in17, in18, in19, in20, in21, in22, in23, in24, in25, in26, in27, in28, in29, in30, in31
  // Probe on Result
  // Probe on PC_out
  Multiplexer #(.select(5), .width(16)) multiplexer_6 (
    .in11({PC_in[15:12], Temp_in[11:0]}), .out(PC_out), .sel(ALUOp[4:0]));  // open: in0, in1, in2, in3, in4, in5, in6, in7, in8, in9, in10, in12, in13, in14, in15, in16, in17, in18, in19, in20, in21, in22, in23, in24, in25, in26, in27, in28, in29, in30, in31
  // Probe on Result
  // Probe on CF_out
  Multiplexer #(.select(5)) multiplexer_7 (
    .in1(addCF_out), .in2(subCF_out), .in8(A[0]), .in9(A[3]), .in10(bcdCF_out), .in12(1'b1), .in13(1'b0),
    .out(CF_out), .sel(ALUOp[4:0]));  // open: in0, in3, in4, in5, in6, in7, in11, in14, in15, in16, in17, in18, in19, in20, in21, in22, in23, in24, in25, in26, in27, in28, in29, in30, in31
  Multiplexer #(.select(5), .width(16)) multiplexer_8 (
    .in11({16{1'b0}}), .out(Temp_out), .sel(ALUOp[4:0]));  // open: in0, in1, in2, in3, in4, in5, in6, in7, in8, in9, in10, in12, in13, in14, in15, in16, in17, in18, in19, in20, in21, in22, in23, in24, in25, in26, in27, in28, in29, in30, in31
  // Probe on Temp_out

  // Other names for the same wires on the sheet: rotlcRes[3:0] = {A[2:0], CF_in}; rotlRes[3:0] = {A[2:0], A[3]};
  //   rotrcCF_out = A[0]; rotrRes[3:0] = {A[0], A[3:1]}; rotrcRes[3:0] = {CF_in, A[3:1]}; rotlcCF_out = A[3];
  //   subCF_in[0] = CF_in

  // Notes on the sheet:
  //   Input
  //   bcd:
  //   for ret:
  //   Output
endmodule

module maindecoder (
  input  [7:0] InstCode,
  input  in_2,
  input  [15:0] PC,
  output [5:0] ALUOp,
  output [2:0] ALUSrcA,
  output [2:0] ALUSrcB,
  output CFRead,
  output CFWrite,
  output ACCWrite,
  output [3:0] ACCWriteSrc,
  output [3:0] RegRead,
  output [3:0] RegWrite,
  output [1:0] RegWriteSrc,
  output [1:0] MemWrite,
  output [1:0] MemWriteSrc,
  output PCWrite,
  output [1:0] PCWriteSrc,
  output [2:0] BranchCond,
  output [1:0] TempWrite,
  output IsABCD,
  output [3:0] ImmA,
  output [3:0] ImmB,
  output Is2ByteInst,
  output In2ndByteState,
  output [7:0] BranchImm,
  output [7:0] InstCodeHigh
);

  wire acc_imm, add_imm, add_mba, addc_mba, and_1_out, and_3_out, and_4_out, and_ba, and_imm, and_mba, bcd,
       clr_cf, clr_ei, comparator_1_gt, comparator_2_gt, comparator_3_eq, comparator_9_eq, comparator_10_eq,
       comparator_11_eq, comparator_12_eq, comparator_13_eq, comparator_19_eq, comparator_20_eq,
       comparator_21_eq, comparator_22_eq, comparator_23_eq, comparator_34_eq, comparator_35_gt,
       comparator_36_lt, comparator_37_eq, comparator_38_gt, comparator_39_lt, comparator_60_gt,
       comparator_61_lt, comparator_62_gt, comparator_63_lt, comparator_66_eq, comparator_67_eq,
       comparator_68_eq, comparator_69_eq, comparator_70_eq, comparator_71_eq, comparator_72_eq,
       comparator_73_eq, comparator_74_eq, comparator_75_eq, dec, dec_mba, dec_mdc, dec_reg, from_mba,
       from_mdc, from_reg, from_timerh, from_timerl, ImmFromFirst, ImmFromSecond, inc, inc_mba, inc_mdc,
       inc_reg, InFirstByte, InFirstByteState, IsBranchInst, nop, or_ba, or_imm, or_mba, r4_imm, rarb_imm,
       rcrd_imm, ret, retc, rotl, rotlc, rotr, rotrc, set_cf, set_ei, shutdown, sub_imm, sub_mba, subc_mba,
       timer_end, timer_imm, timer_start, to_ioa, to_iob, to_ioc, to_mba, to_mdc, to_reg, to_timerh,
       to_timerl, xor_ba, xor_imm, xor_mba;
  wire [3:0] multiplexer_2_out;
  wire [7:0] FirstByteReg, SecondByteReg, undriven;

  // Probe on InstCodeHigh
  Comparator #(.mode("unsigned")) comparator_1 (.a(InstCodeHigh), .b(8'h79), .gt(comparator_1_gt));  // open: eq, lt
  Comparator #(.mode("unsigned")) comparator_2 (.a(InstCodeHigh), .b({8{1'b1}}), .gt(comparator_2_gt));  // open: eq, lt
  Comparator #(.mode("unsigned")) comparator_3 (.a(InstCodeHigh), .b({8{1'b1}}), .eq(comparator_3_eq));  // open: gt, lt
  // Probe on InstCode[7:4]
  Register #(.width(1)) InSecondByteState (
    .D(InFirstByteState), .en(1'b1), .clk(in_2), .Q(In2ndByteState));  // open: clr
  Register FirstByte_Reg (.D(InstCode), .en(InFirstByteState), .clk(in_2), .Q(FirstByteReg));  // open: clr
  Multiplexer #(.width(8)) multiplexer_1 (.in1(InstCode), .out(SecondByteReg), .sel(and_1_out));  // open: in0
  and and_1 (and_1_out, In2ndByteState, 1'b1);
  Comparator #(.width(4)) comparator_4 (.a(InstCode[7:4]), .b(4'b0111), .eq(ImmFromFirst));  // open: gt, lt
  Comparator comparator_5 (.a(InstCodeHigh), .b(8'h8), .eq(addc_mba));  // open: gt, lt
  Comparator comparator_6 (.a(InstCodeHigh), .b(8'h9), .eq(add_mba));  // open: gt, lt
  Comparator comparator_7 (.a(InstCodeHigh), .b(8'hc), .eq(inc_mba));  // open: gt, lt
  Comparator comparator_8 (.a(InstCodeHigh), .b(8'he), .eq(inc_mdc));  // open: gt, lt
  Comparator comparator_9 (.a(InstCodeHigh), .b(8'h10), .eq(comparator_9_eq));  // open: gt, lt
  Comparator comparator_10 (.a(InstCodeHigh), .b(8'h12), .eq(comparator_10_eq));  // open: gt, lt
  or or_1 (inc_reg, comparator_9_eq, comparator_10_eq, comparator_11_eq, comparator_12_eq, comparator_13_eq);
  Comparator comparator_11 (.a(InstCodeHigh), .b(8'h14), .eq(comparator_11_eq));  // open: gt, lt
  Comparator comparator_12 (.a(InstCodeHigh), .b(8'h16), .eq(comparator_12_eq));  // open: gt, lt
  Comparator comparator_13 (.a(InstCodeHigh), .b(8'h18), .eq(comparator_13_eq));  // open: gt, lt
  Comparator comparator_14 (.a(InstCodeHigh), .b(8'h31), .eq(inc));  // open: gt, lt
  Comparator comparator_15 (.a(InstCodeHigh), .b(8'ha), .eq(subc_mba));  // open: gt, lt
  Comparator comparator_16 (.a(InstCodeHigh), .b(8'hb), .eq(sub_mba));  // open: gt, lt
  Comparator comparator_17 (.a(InstCodeHigh), .b(8'hd), .eq(dec_mba));  // open: gt, lt
  Comparator comparator_18 (.a(InstCodeHigh), .b(8'hf), .eq(dec_mdc));  // open: gt, lt
  Comparator comparator_19 (.a(InstCodeHigh), .b(8'h11), .eq(comparator_19_eq));  // open: gt, lt
  Comparator comparator_20 (.a(InstCodeHigh), .b(8'h13), .eq(comparator_20_eq));  // open: gt, lt
  or or_2 (dec_reg, comparator_19_eq, comparator_20_eq, comparator_21_eq, comparator_22_eq, comparator_23_eq);
  Comparator comparator_21 (.a(InstCodeHigh), .b(8'h15), .eq(comparator_21_eq));  // open: gt, lt
  Comparator comparator_22 (.a(InstCodeHigh), .b(8'h17), .eq(comparator_22_eq));  // open: gt, lt
  Comparator comparator_23 (.a(InstCodeHigh), .b(8'h19), .eq(comparator_23_eq));  // open: gt, lt
  Comparator comparator_24 (.a(InstCodeHigh), .b(8'h3f), .eq(dec));  // open: gt, lt
  Comparator comparator_25 (.a(InstCodeHigh), .b(8'h3a), .eq(from_timerl));  // open: gt, lt
  Comparator comparator_26 (.a(InstCodeHigh), .b(8'h3b), .eq(from_timerh));  // open: gt, lt
  Comparator comparator_27 (.a(InstCodeHigh), .b(8'h40), .eq(add_imm));  // open: gt, lt
  Comparator comparator_28 (.a(InstCodeHigh), .b(8'h41), .eq(sub_imm));  // open: gt, lt
  Comparator comparator_29 (.a(InstCodeHigh), .b(8'h42), .eq(and_imm));  // open: gt, lt
  Comparator comparator_30 (.a(InstCodeHigh), .b(8'h43), .eq(xor_imm));  // open: gt, lt
  Comparator comparator_31 (.a(InstCodeHigh), .b(8'h44), .eq(or_imm));  // open: gt, lt
  Comparator comparator_32 (.a(InstCodeHigh), .b(8'h46), .eq(r4_imm));  // open: gt, lt
  Comparator comparator_33 (.a(InstCodeHigh), .b(8'h47), .eq(timer_imm));  // open: gt, lt
  // Probe on InstCode
  not not_1 (InFirstByte, In2ndByteState);
  // Probe on SecondByteReg
  // Probe on InstCode[7:4]
  // Probe on InstCode[7:4]
  and and_2 (ImmFromSecond, In2ndByteState, 1'b1);
  or or_3 (IsBranchInst, comparator_1_gt, comparator_2_gt, comparator_3_eq);
  Comparator #(.mode("unsigned")) comparator_34 (.a(InstCode), .b(8'h37), .eq(comparator_34_eq));  // open: gt, lt
  Comparator #(.mode("unsigned"), .width(4)) comparator_35 (
    .a(InstCode[7:4]), .b(4'b0011), .gt(comparator_35_gt));  // open: eq, lt
  Comparator #(.mode("unsigned"), .width(4)) comparator_36 (
    .a(InstCode[7:4]), .b(4'b0111), .lt(comparator_36_lt));  // open: gt, eq
  Comparator #(.mode("unsigned"), .width(4)) comparator_37 (
    .a(InstCode[7:4]), .b(4'b1111), .eq(comparator_37_eq));  // open: gt, lt
  Comparator #(.mode("unsigned"), .width(4)) comparator_38 (
    .a(InstCode[7:4]), .b(4'b0111), .gt(comparator_38_gt));  // open: eq, lt
  Comparator #(.mode("unsigned"), .width(4)) comparator_39 (
    .a(InstCode[7:4]), .b(4'b1111), .lt(comparator_39_lt));  // open: gt, eq
  and and_3 (and_3_out, comparator_35_gt, comparator_36_lt);
  and and_4 (and_4_out, comparator_38_gt, comparator_39_lt);
  Comparator comparator_40 (.a(InstCodeHigh), .b({8{1'b0}}), .eq(rotr));  // open: gt, lt
  Comparator comparator_41 (.a(InstCodeHigh), .b(8'h1), .eq(rotl));  // open: gt, lt
  Comparator comparator_42 (.a(InstCodeHigh), .b(8'h2), .eq(rotrc));  // open: gt, lt
  Comparator comparator_43 (.a(InstCodeHigh), .b(8'h3), .eq(rotlc));  // open: gt, lt
  Comparator comparator_44 (.a(InstCodeHigh), .b(8'h4), .eq(from_mba));  // open: gt, lt
  Comparator comparator_45 (.a(InstCodeHigh), .b(8'h5), .eq(to_mba));  // open: gt, lt
  Comparator comparator_46 (.a(InstCodeHigh), .b(8'h6), .eq(from_mdc));  // open: gt, lt
  Comparator comparator_47 (.a(InstCodeHigh), .b(8'h7), .eq(to_mdc));  // open: gt, lt
  Comparator comparator_48 (.a(InstCodeHigh), .b(8'h1a), .eq(and_ba));  // open: gt, lt
  Comparator comparator_49 (.a(InstCodeHigh), .b(8'h1d), .eq(and_mba));  // open: gt, lt
  Comparator comparator_50 (.a(InstCodeHigh), .b(8'h1b), .eq(xor_ba));  // open: gt, lt
  Comparator comparator_51 (.a(InstCodeHigh), .b(8'h1e), .eq(xor_mba));  // open: gt, lt
  Comparator comparator_52 (.a(InstCodeHigh), .b(8'h1c), .eq(or_ba));  // open: gt, lt
  Comparator comparator_53 (.a(InstCodeHigh), .b(8'h1f), .eq(or_mba));  // open: gt, lt
  Comparator comparator_54 (.a(InstCodeHigh), .b(8'h2a), .eq(clr_cf));  // open: gt, lt
  Comparator comparator_55 (.a(InstCodeHigh), .b(8'h2b), .eq(set_cf));  // open: gt, lt
  Comparator comparator_56 (.a(InstCodeHigh), .b(8'h2c), .eq(set_ei));  // open: gt, lt
  Comparator comparator_57 (.a(InstCodeHigh), .b(8'h2d), .eq(clr_ei));  // open: gt, lt
  Comparator comparator_58 (.a(InstCodeHigh), .b(8'h3c), .eq(to_timerl));  // open: gt, lt
  Comparator comparator_59 (.a(InstCodeHigh), .b(8'h3d), .eq(to_timerh));  // open: gt, lt
  Comparator comparator_60 (.a(InstCodeHigh), .b(8'h4f), .gt(comparator_60_gt));  // open: eq, lt
  Comparator comparator_61 (.a(InstCodeHigh), .b(8'h60), .lt(comparator_61_lt));  // open: gt, eq
  Comparator comparator_62 (.a(InstCodeHigh), .b(8'h5f), .gt(comparator_62_gt));  // open: eq, lt
  Comparator comparator_63 (.a(InstCodeHigh), .b(8'h70), .lt(comparator_63_lt));  // open: gt, eq
  Comparator #(.width(4)) comparator_64 (.a(InstCode[7:4]), .b(4'b0111), .eq(acc_imm));  // open: gt, lt
  Comparator comparator_65 (.a(InstCodeHigh), .b(8'h37), .eq(shutdown));  // open: gt, lt
  or or_4 (Is2ByteInst, comparator_34_eq, and_3_out, comparator_37_eq, and_4_out);
  Multiplexer #(.width(4)) multiplexer_2 (.in1(InstCode[3:0]), .out(multiplexer_2_out), .sel(IsABCD));  // open: in0
  and and_5 (rarb_imm, comparator_60_gt, comparator_61_lt);
  and and_6 (rcrd_imm, comparator_62_gt, comparator_63_lt);
  and and_7 (InFirstByteState, InFirstByte, Is2ByteInst);
  // Probe on InstCodeHigh
  Multiplexer #(.width(8)) multiplexer_3 (.in0(InstCode), .in1(FirstByteReg), .out(InstCodeHigh), .sel(In2ndByteState));
  // Probe on ImmA
  Multiplexer #(.width(4)) multiplexer_4 (.in1(InstCode[3:0]), .out(ImmA), .sel(ImmFromFirst));  // open: in0
  Multiplexer #(.width(4)) multiplexer_5 (
    .in0(multiplexer_2_out), .in1(SecondByteReg[3:0]), .out(ImmB), .sel(ImmFromSecond));
  // Probe on BranchImm
  Multiplexer #(.width(8)) multiplexer_6 (.in0(undriven), .in1(SecondByteReg), .out(BranchImm), .sel(IsBranchInst));
  // Probe on ImmB
  Comparator comparator_66 (.a(InstCodeHigh), .b(8'h20), .eq(comparator_66_eq));  // open: gt, lt
  Comparator comparator_67 (.a(InstCodeHigh), .b(8'h22), .eq(comparator_67_eq));  // open: gt, lt
  or or_5 (to_reg, comparator_66_eq, comparator_67_eq, comparator_68_eq, comparator_69_eq, comparator_70_eq);
  Comparator comparator_68 (.a(InstCodeHigh), .b(8'h24), .eq(comparator_68_eq));  // open: gt, lt
  Comparator comparator_69 (.a(InstCodeHigh), .b(8'h26), .eq(comparator_69_eq));  // open: gt, lt
  Comparator comparator_70 (.a(InstCodeHigh), .b(8'h28), .eq(comparator_70_eq));  // open: gt, lt
  Comparator comparator_71 (.a(InstCodeHigh), .b(8'h21), .eq(comparator_71_eq));  // open: gt, lt
  Comparator comparator_72 (.a(InstCodeHigh), .b(8'h23), .eq(comparator_72_eq));  // open: gt, lt
  or or_6 (from_reg, comparator_71_eq, comparator_72_eq, comparator_73_eq, comparator_74_eq, comparator_75_eq);
  Comparator comparator_73 (.a(InstCodeHigh), .b(8'h25), .eq(comparator_73_eq));  // open: gt, lt
  Comparator comparator_74 (.a(InstCodeHigh), .b(8'h27), .eq(comparator_74_eq));  // open: gt, lt
  Comparator comparator_75 (.a(InstCodeHigh), .b(8'h29), .eq(comparator_75_eq));  // open: gt, lt
  Comparator comparator_76 (.a(InstCodeHigh), .b(8'h2e), .eq(ret));  // open: gt, lt
  Comparator comparator_77 (.a(InstCodeHigh), .b(8'h2f), .eq(retc));  // open: gt, lt
  Comparator comparator_78 (.a(InstCodeHigh), .b(8'h32), .eq(to_ioa));  // open: gt, lt
  Comparator comparator_79 (.a(InstCodeHigh), .b(8'h33), .eq(to_iob));  // open: gt, lt
  Comparator comparator_80 (.a(InstCodeHigh), .b(8'h34), .eq(to_ioc));  // open: gt, lt
  Comparator comparator_81 (.a(InstCodeHigh), .b(8'h36), .eq(bcd));  // open: gt, lt
  Comparator comparator_82 (.a(InstCodeHigh), .b(8'h38), .eq(timer_start));  // open: gt, lt
  Comparator comparator_83 (.a(InstCodeHigh), .b(8'h39), .eq(timer_end));  // open: gt, lt
  Comparator comparator_84 (.a(InstCodeHigh), .b(8'h3e), .eq(nop));  // open: gt, lt
  ROM #(.dataWidth(42)) rom_1 (
    .addr(InstCodeHigh),
    .data({ALUOp, ALUSrcA, ALUSrcB, CFRead, CFWrite, ACCWrite, ACCWriteSrc, RegRead, RegWrite, RegWriteSrc, MemWrite, MemWriteSrc, PCWrite, PCWriteSrc, BranchCond, TempWrite, IsABCD}));

  // Other names for the same wires on the sheet: Clk = in_2; CurInstCode[7:0] = InstCode;
  //   LoNibble[3:0] = InstCode[3:0]; HiNibble[3:0] = InstCode[7:4]; InstCode_t[7:0] = InstCodeHigh;
  //   lnSecondByteState = In2ndByteState

  // Notes on the sheet:
  //   acc
  //   add
  //   sub
  //   2-byte instructions:
  //   (first bytes)
  //   Input
  //   and
  //   xor
  //   or
  //   2-Byte Instruction Logic
  //   imm setting!
  //   Instruction Decoding!!!!!!!
  //   discard.....rip hardwork........
  //   rot
  //   ret
  //   contents of rom_1 (hex, n*v repeats v):
  //   6019000100 7019000100 8039000100 9039000100 8000100 d00 48800100 1500 1139000100 1119000100
  //   2139000100 2119000100 12c0000b00 22c0000b00 14c0001300 24c0001300 16c008a100 26c008a100 16c0112100
  //   26c0112100 16c019a100 26c019a100 16c0222100 26c0222100 16c02aa100 26c02aa100 3119000100 4119000100
  //   5119000100 3110000b00 4110000b00 5110000b00 8100 9880100 10100 9900100 18100 9980100 20100 9a00100
  //   28100 9a80100 d010000100 c010000100 0 0 b8000001c4 0 0 10d9000100 1ab00100 0 0 0 a039000100 7*0
  //   1000100 20d9000100 1099000140 2099000140 3099000140 4099000140 5099000140 0 2c140 9*0 16*34141
  //   16*3c141 16*a000100 32*181 8*80198 8*1001a0 8*188 8*190 8*1a8 8*1b0 8*1689200190 16*180
  //   16*16c9000182
  //   Output
endmodule

module PCReg (
  input  Clk,
  input  PCSel,
  input  [15:0] BranchAddr,
  input  [15:0] IncValue,
  input  IsRet,
  input  [15:0] AluTempOut,
  output [15:0] PC_Out,
  output [3:0] PC_Hi4
);

  wire [15:0] multiplexer_1_out, multiplexer_2_out, PC_Plus;

  // Probe on PC_Plus
  Multiplexer #(.width(16)) multiplexer_1 (.in0(PC_Plus), .in1(BranchAddr), .out(multiplexer_1_out), .sel(PCSel));
  // Probe on BranchAddr
  // Probe on multiplexer_1_out
  Multiplexer #(.width(16)) multiplexer_2 (
    .in0(multiplexer_1_out), .in1(AluTempOut), .out(multiplexer_2_out), .sel(IsRet));
  Register #(.width(16)) PC_Reg (.D(multiplexer_2_out), .en(1'b1), .clk(Clk), .Q({PC_Hi4, PC_Out[11:0]}));  // open: clr
  // Probe on {PC_Hi4, PC_Out[11:0]}
  Adder #(.width(16)) adder_1 (.a({PC_Hi4, PC_Out[11:0]}), .b(16'h1), .out(PC_Plus));  // open: cin, cout

  assign PC_Out[15:12] = PC_Hi4;

  // Other names for the same wires on the sheet: Clock = Clk

  // Notes on the sheet:
  //   Input
  //   Output
endmodule

module Timer (
  input  Input,
  input  in_2,
  input  in_3,
  input  in_4,
  input  [3:0] in_5,
  input  in_6,
  output [7:0] Output,
  output out_8
);

  wire IncOnly, IncrementNow, IsCount3, LoadAny, NotLoadAny, Plus1_Cout;
  wire [1:0] CycleCount_plus1, CycleCount_Reg_q, multiplexer_1_out;
  wire [7:0] HoldOrInc, LoadFromACC, NextTimerVal, TIMER_plus1;

  Register Timer_Reg (.clk(in_6), .Q(Output));  // open: D, en, clr
  Multiplexer #(.width(2)) multiplexer_1 (.in0(2'b00), .in1(CycleCount_plus1), .out(multiplexer_1_out), .sel(Input));
  and and_1 (IncrementNow, IsCount3, Input);
  Adder adder_1 (.a(Output), .b(8'h1), .out(TIMER_plus1), .cout(Plus1_Cout));  // open: cin
  or or_1 (LoadAny, in_3, in_4);
  Multiplexer #(.width(8)) multiplexer_2 (.in0(Output), .in1(TIMER_plus1), .out(HoldOrInc), .sel(IncOnly));
  Register #(.width(2)) CycleCount_Reg (.D(multiplexer_1_out), .clk(in_6), .Q(CycleCount_Reg_q));  // open: en, clr
  not not_1 (NotLoadAny, LoadAny);
  Multiplexer #(.width(8)) multiplexer_3 (.in0(HoldOrInc), .in1(LoadFromACC), .out(NextTimerVal), .sel(LoadAny));
  Multiplexer #(.width(4)) multiplexer_4 (.in0(Output[7:4]), .in1(in_5), .out(LoadFromACC[7:4]), .sel(in_3));
  Adder #(.width(2)) adder_2 (.a(CycleCount_Reg_q), .b(2'b01), .out(CycleCount_plus1));  // open: cin, cout
  Comparator #(.width(2)) comparator_1 (.a(CycleCount_Reg_q), .b(2'b11), .eq(IsCount3));  // open: gt, lt
  and and_2 (IncOnly, NotLoadAny, IncrementNow);
  and and_3 (out_8, IncrementNow, Plus1_Cout);
  Multiplexer #(.width(4)) multiplexer_5 (.in0(Output[3:0]), .in1(in_5), .out(LoadFromACC[3:0]), .sel(in_4));

  // Other names for the same wires on the sheet: ACC_in[3:0] = in_5; Clock = in_6; NextHi[3:0] = LoadFromACC[3:0];
  //   NextLo[3:0] = LoadFromACC[7:4]; TIMER_Hi[3:0] = Output[3:0]; Timer_out[7:0] = Output; Timer_RegQ[7:0] = Output;
  //   TIMER_Lo[3:0] = Output[7:4]; TimerEnd = in_2; TimerOverflow = out_8; TimerStart = Input; ToTimerHi = in_4;
  //   ToTimerLo = in_3
endmodule

module DataMem (
  input  [7:0] Addr,
  input  [1:0] MemWrite,
  input  [3:0] Data_in,
  input  Clk,
  output [3:0] Data_out
);

  wire comparator_1_eq, WE;

  not not_1 (WE, comparator_1_eq);
  Comparator #(.width(2)) comparator_1 (.a(MemWrite), .b(2'b00), .eq(comparator_1_eq));  // open: gt, lt
  RAM #(.asyncread("true"), .dataWidth(4)) DataMem (
    .addr(Addr), .we(WE), .oe(1'b1), .clk(Clk), .din(Data_in), .dout(Data_out));
endmodule

module PCLogic (
  input  [15:0] PCIn,
  input  [15:0] InstrWord,
  input  [3:0] ACC_out,
  input  CF_out,
  input  [3:0] RegA_out,
  input  [3:0] RegB_out,
  input  [15:0] TEMP_out,
  input  Is2ByteInst,
  input  Prelim_PCSel,
  input  TempRead,
  input  [2:0] BranchType,
  input  Is2ndByteState,
  input  is_bbit,
  input  is_b,
  input  is_call,
  output [15:0] IncValue,
  output [15:0] BranchTarget,
  output PCSel
);

  wire ACC_isZero, ACC_notZero, and_1_out, and_2_out, and_3_out, and_4_out, and_5_out, and_6_out, and_7_out,
       BBitSatisfied, CF_isZero, CondTrue, is_bcall, multiplexer_5_out, RegA_isZero, RegA_notZero,
       RegB_isZero, RegB_notZero;
  wire [15:0] BranchAddrA, BranchAddrB, Pre_IncValue;

  // Probe on InstrWord
  // Probe on PCIn[15:11]
  // Probe on InstrWord[10:0]
  // Probe on {PCIn[15:11], InstrWord[10:0]}
  Multiplexer #(.width(16)) multiplexer_1 (.in0(16'h1), .in1(16'h1), .out(Pre_IncValue), .sel(Is2ByteInst));
  Multiplexer #(.width(16)) multiplexer_2 (.in0(Pre_IncValue), .in1(16'h1), .out(IncValue), .sel(Is2ndByteState));
  not not_1 (CF_isZero, CF_out);
  nor nor_1 (ACC_isZero, ACC_out[0], ACC_out[1], ACC_out[2], ACC_out[3]);
  nor nor_2 (RegA_isZero, RegA_out[0], RegA_out[1], RegA_out[2], RegA_out[3]);
  nor nor_3 (RegB_isZero, RegB_out[0], RegB_out[1], RegB_out[2], RegB_out[3]);
  // Probe on PCIn[15:12]
  // Probe on InstrWord[11:0]
  not not_2 (ACC_notZero, ACC_isZero);
  not not_3 (RegA_notZero, RegA_isZero);
  not not_4 (RegB_notZero, RegB_isZero);
  or or_1 (is_bcall, is_call, is_b);
  // Probe on {PCIn[15:12], InstrWord[11:0]}
  // Probe on IncValue
  Adder #(.width(16)) adder_1 (.a(IncValue), .b({16{1'b0}}), .out(BranchAddrA));  // open: cin, cout
  Multiplexer #(.width(16)) multiplexer_3 (
    .in0({PCIn[15:11], InstrWord[10:0]}), .in1({PCIn[15:12], InstrWord[11:0]}), .out(BranchAddrB),
    .sel(is_bcall));
  and and_1 (and_1_out, Prelim_PCSel, BBitSatisfied);
  // Probe on BranchType
  and and_2 (and_2_out, Prelim_PCSel, CondTrue);
  and and_3 (and_3_out, Prelim_PCSel, is_bcall);
  and and_4 (and_4_out, and_1_out, Is2ndByteState);
  // Probe on InstrWord[12:11]
  Multiplexer #(.select(3)) multiplexer_4 (
    .in0(1'b0), .in1(ACC_isZero), .in2(ACC_notZero), .in3(RegA_notZero), .in4(RegB_notZero), .in5(CF_isZero),
    .in6(CF_out), .in7(1'b1), .out(CondTrue), .sel(BranchType));
  and and_5 (and_5_out, and_2_out, Is2ndByteState);
  and and_6 (and_6_out, and_3_out, Is2ndByteState);
  Multiplexer #(.select(2)) multiplexer_5 (
    .in0(ACC_out[0]), .in1(ACC_out[1]), .in2(ACC_out[2]), .in3(ACC_out[3]), .out(multiplexer_5_out),
    .sel(InstrWord[12:11]));
  // Probe on BranchTarget
  Multiplexer #(.width(16)) multiplexer_6 (
    .in0(BranchAddrA), .in1(BranchAddrB), .out(BranchTarget), .sel(Is2ndByteState));
  and and_7 (and_7_out, and_4_out, is_bbit);
  Comparator #(.width(1)) comparator_1 (.a(multiplexer_5_out), .b(1'b1), .eq(BBitSatisfied));  // open: gt, lt
  // Probe on BranchTarget
  or or_2 (PCSel, and_5_out, and_6_out, and_7_out);

  // Other names for the same wires on the sheet: BranchAddrB_4[15:0] = {PCIn[15:12], InstrWord[11:0]};
  //   BranchAddrB_5[15:0] = {PCIn[15:11], InstrWord[10:0]}; Instr_low11[10:0] = InstrWord[10:0];
  //   Instr_low12[11:0] = InstrWord[11:0]; KK[1:0] = InstrWord[12:11]; PC_Hi4[3:0] = PCIn[15:12];
  //   PC_Hi5[4:0] = PCIn[15:11]; PC_in[15:0] = PCIn; CF_notZero = CF_out

  // Notes on the sheet:
  //   Input
  //   Output
  //   branch and b-bit
  //   call and b
  //   b-bit condition checking
endmodule
